// Logisim project exampleCounter.circ as structural Verilog: 1 circuit, main circuit main
module main (
);

  wire clock_1_out;
  wire [1:0] JK_0_q;

  Clock clock_1 (.out(clock_1_out));
  J_K_Flip_Flop JK_0 (.J(1'b1), .clk(clock_1_out), .K(1'b1), .Q(JK_0_q[0]));  // open: Qn, preset, en, reset
  J_K_Flip_Flop JK_1 (.J(JK_0_q[0]), .clk(clock_1_out), .K(JK_0_q[0]), .Q(JK_0_q[1]));  // open: Qn, preset, en, reset
  Hex_Digit_Display hex_digit_display_1 (.value({2'b00, JK_0_q}));  // open: dp
endmodule
