// Logisim project exerciseCount.circ as structural Verilog: 1 circuit, main circuit main
module main (
);

  wire JK_0_q, JK_0_qn, JK_1_q, JK_1_qn, Taktsignal_out;
  wire [2:0] Y0_out;

  Clock Taktsignal (.out(Taktsignal_out));
  J_K_Flip_Flop JK_0 (.J(1'b1), .clk(Taktsignal_out), .K(1'b1), .Q(JK_0_q), .Qn(JK_0_qn));  // open: preset, en, reset
  J_K_Flip_Flop JK_1 (
    .J(JK_0_q), .clk(Taktsignal_out), .K(JK_0_q), .Q(JK_1_q), .Qn(JK_1_qn));  // open: preset, en, reset
  and Y0 (Y0_out[0], JK_1_qn, JK_0_qn);
  and Y1 (Y0_out[1], JK_0_q, JK_1_q);
  and Y2 (Y0_out[2], JK_0_q, JK_1_qn);
  Hex_Digit_Display hex_digit_display_1 (.value({1'b0, Y0_out}));  // open: dp
endmodule
